# Fritzing sketch Circuito_fritzing (saved by Fritzing 0.9.3b)
circuit board: 7.93235cm x 7.86759cm
breadboards: 2

parts:
  Q1 = NPN-Transistor [package="TO92 [THT]"]
  Q2 = Basic FET P-Channel [package="TO220 [THT]"]
  D1 = Rectifier Diode [part_number=1N4001 package="300 mil [THT]"]
  SPPM = Screw terminal - 2 pins [package=THT]
  R1 = Resistor [tolerance=±5% resistance=220 package=THT]
  R2 = Resistor [tolerance=±5% resistance=220 package=THT]
  Componente1 = Arduino Pro Mini (5V)
  5V = Screw terminal - 2 pins [package=THT]
  BMS = Screw terminal - 2 pins [package=THT]
  Componente2 = ACS712 Low Current Sensor Board v12
  R3 = Resistor [tolerance=±5% resistance=33k package=THT]
  C1 = Ceramic Capacitor [capacitance=100nF package="100 mil [THT, multilayer]"]
  Q3 = NPN-Transistor [package="TO92 [THT]"]
  Q4 = Basic FET P-Channel [package="TO220 [THT]"]
  R4 = Resistor [tolerance=±5% resistance=220 package=THT]
  R5 = Resistor [tolerance=±5% resistance=220 package=THT]
  U1 = POT [package=3362u]
  IC2 = IC, DIP package, 8 pins [chip_label=TLC272]
  R7 = TRIMPOT [package=3386u]
  R8 = TRIMPOT [package=3386u]
  R9 = Resistor [tolerance=±5% resistance=220 package=THT]
  S1 = Pushbutton [package="[THT]"]
  D6 = Rectifier Diode [part_number=1N4001 package="300 mil [THT]"]
  D7 = Rectifier Diode [part_number=1N4001 package="300 mil [THT]"]
  D8 = Rectifier Diode [part_number=1N4001 package="300 mil [THT]"]
  LED1 = LED - 5mm [color="Red (633nm)" package="5 mm [THT]"]
  R10 = Resistor [tolerance=±5% resistance=330 package=THT]
  Carga = Screw terminal - 2 pins [package=THT]
  Grove1 = Grove OLED 128x96
  R11 = Resistor [tolerance=±5% resistance=33k package=THT]
  C2 = Ceramic Capacitor [capacitance=100nF package="100 mil [THT, multilayer]"]
  LM35 = Header 3 [package=molex-1x3_lock]

nets:
  N1: Q1.E, Q2.gate, R2.Pin_1
  N2: Q1.B, R1.Pin_0
  GND: Q1.C, SPPM.pin2, Componente1.GND, 5V.pin1, BMS.pin2, Componente2.GND, C1.1, Q3.C, U1.A, IC2.pin4, R7.CCW, R8.CCW, R9.Pin_1, LED1.cathode, Carga.pin2, Grove1.GND, C2.1, LM35.3
  N3: Q2.drain, D1.anode, U1.E
  N4: Q2.source, SPPM.pin1
  N5: D1.cathode, Componente2.IP+
  N6: R1.Pin_1, Componente1.D5
  N7: R2.Pin_0, BMS.pin1, Componente2.IP-, Q4.source, R5.Pin_0
  VCC: Componente1.VCC, 5V.pin2, Componente2.VO, IC2.pin8, R7.CW, R8.CW, S1.Pin_1, S1.Pin_2, Grove1.VCC, LM35.1
  N8: Componente1.A4, Grove1.SDA
  N9: Componente1.A5, Grove1.SCL
  N10: Componente1.A2, U1.S, IC2.pin5
  N11: Componente1.A0, R3.Pin_1, C1.0
  N12: Componente1.SCK, R10.Pin_0
  N13: Componente1.D6, R4.Pin_1
  N14: Componente1.D3, D6.cathode, D7.cathode, D8.cathode
  N15: Componente1.D2, R9.Pin_0, S1.Pin_3, S1.Pin_4, D6.anode
  N16: Componente2.5V, R3.Pin_0, IC2.pin3
  N17: Q3.E, Q4.gate, R5.Pin_1
  N18: Q3.B, R4.Pin_0
  N19: Q4.drain, Carga.pin1
  N20: IC2.pin1, D8.anode
  N21: IC2.pin2, R7.WIPER
  N22: IC2.pin6, R8.WIPER
  N23: IC2.pin7, D7.anode
  N24: LED1.anode, R10.Pin_1
  N25: R11.Pin_0, LM35.2
  N26: R11.Pin_1, C2.0
